// Logisim project S1-T14.circ as structural Verilog: 7 circuits, main circuit main
module main (
  input  _1,
  input  Q1,
  input  Q2,
  input  _1_2,
  input  Q3,
  input  Q4,
  input  Q5,
  input  Q6,
  input  in_9,
  input  _0,
  input  Q7,
  input  in_12,
  input  _0_2,
  input  Q8,
  input  in_15,
  input  Q9,
  input  Q10,
  input  _0_3,
  input  _0_4,
  input  _0_5,
  input  _1_3,
  input  _0_6,
  input  in_23,
  input  in_24,
  input  in_25,
  input  in_26,
  input  _0_7,
  input  _0_8,
  input  _0_9,
  input  _0_10,
  input  _0_11,
  input  _1_4,
  input  _0_12,
  input  _0_13,
  input  _1_5,
  input  _0_14,
  input  _0_15,
  input  in_38,
  input  _1_6,
  input  _0_16,
  input  _1_7,
  input  _0_17,
  input  _0_18,
  input  _0_19,
  input  _0_20,
  input  _0_21,
  input  Move_to_next_Question,
  input  in_48,
  input  Clear___0,
  input  RESET,
  output out_51,
  output out_52,
  output out_53,
  output out_54,
  output Correct_Answer,
  output out_56,
  output out_57,
  output out_58,
  output out_59,
  output out_60,
  output out_61,
  output out_62,
  output Result,
  output out_64,
  output out_65,
  output out_66,
  output out_67,
  output out_68,
  output out_69,
  output out_70,
  output out_71,
  output out_72,
  output Question_Number,
  output out_74,
  output out_75
);

  wire and_1_out, and_2_out, and_3_out, and_4_out, and_5_out, and_6_out, and_7_out, and_8_out, and_9_out,
       and_10_out, and_11_out, and_16_out, and_17_out, and_18_out, and_19_out, and_20_out, and_21_out,
       and_22_out, and_23_out, \BCD_Adder_2__2__σ3 , \BCD_Adder_2__6__σ2 , \BCD_Adder_2__9__σ1 ,
       BCD_Adder_2__14__c4, \BCD_Adder_2__15__σ4 , \BCD_Adder__2__σ3 , \BCD_Adder__6__σ2 ,
       \BCD_Adder__9__σ1 , BCD_Adder__14__c4, \BCD_Adder__15__σ4 , bcd_to_7_segment_display_decoder_1_a,
       bcd_to_7_segment_display_decoder_1_b, bcd_to_7_segment_display_decoder_1_c,
       bcd_to_7_segment_display_decoder_1_d, bcd_to_7_segment_display_decoder_1_e,
       bcd_to_7_segment_display_decoder_1_f, bcd_to_7_segment_display_decoder_1_g,
       bcd_to_7_segment_display_decoder_2_a, bcd_to_7_segment_display_decoder_2_b,
       bcd_to_7_segment_display_decoder_2_c, bcd_to_7_segment_display_decoder_2_d,
       bcd_to_7_segment_display_decoder_2_e, bcd_to_7_segment_display_decoder_2_f,
       bcd_to_7_segment_display_decoder_2_g, bcd_to_7_segment_display_decoder_3_a,
       bcd_to_7_segment_display_decoder_3_b, bcd_to_7_segment_display_decoder_3_c,
       bcd_to_7_segment_display_decoder_3_d, bcd_to_7_segment_display_decoder_3_e,
       bcd_to_7_segment_display_decoder_3_f, bcd_to_7_segment_display_decoder_3_g,
       bcd_to_7_segment_display_decoder_4_a, bcd_to_7_segment_display_decoder_4_b,
       bcd_to_7_segment_display_decoder_4_c, bcd_to_7_segment_display_decoder_4_d,
       bcd_to_7_segment_display_decoder_4_e, bcd_to_7_segment_display_decoder_4_f,
       bcd_to_7_segment_display_decoder_4_g, dipswitch_1_p1, dipswitch_1_p2, dipswitch_1_p3, dipswitch_1_p4,
       four_bit_d_ff_1__2__1q, four_bit_d_ff_1__7__2q, four_bit_d_ff_1__10__3q, four_bit_d_ff_1__15__4q,
       four_bit_d_ff_2__2__1q, four_bit_d_ff_2__7__2q, four_bit_d_ff_2__10__3q, four_bit_d_ff_2__15__4q,
       four_bit_d_ff_3__2__1q, four_bit_d_ff_3__7__2q, four_bit_d_ff_3__10__3q, four_bit_d_ff_3__15__4q,
       four_bit_d_ff_4__2__1q, four_bit_d_ff_4__7__2q, four_bit_d_ff_4__10__3q, four_bit_d_ff_4__15__4q,
       four_bit_d_ff_5__2__1q, four_bit_d_ff_5__7__2q, four_bit_d_ff_5__10__3q, four_bit_d_ff_5__15__4q,
       four_bit_d_ff_6__2__1q, four_bit_d_ff_6__7__2q, four_bit_d_ff_6__10__3q, four_bit_d_ff_6__15__4q,
       four_bit_d_ff_7__2__1q, four_bit_d_ff_7__7__2q, four_bit_d_ff_7__10__3q, four_bit_d_ff_7__15__4q,
       four_bit_d_ff_8__2__1q, four_bit_d_ff_8__7__2q, four_bit_d_ff_8__10__3q, four_bit_d_ff_8__15__4q,
       four_bit_d_ff_9__2__1q, four_bit_d_ff_9__7__2q, four_bit_d_ff_9__10__3q, four_bit_d_ff_9__15__4q,
       four_bit_d_ff_10__2__1q, four_bit_d_ff_10__7__2q, four_bit_d_ff_10__10__3q, four_bit_d_ff_10__15__4q,
       j_k_ff_1_qn, j_k_ff_2_qn, j_k_ff_3_qn, \n4_bit_adder_1__2__σ3 , \n4_bit_adder_1__6__σ2 ,
       \n4_bit_adder_1__9__σ1 , \n4_bit_adder_1__15__σ4 , n4_bit_magnitude_comparator_1__5__a_b_out,
       n4_bit_magnitude_comparator_1__6__a_b_out, n4_bit_magnitude_comparator_1__7__a_b_out,
       n4_bit_magnitude_comparator_2__6__a_b_out, not_1_out, not_2_out, not_3_out, not_4_out, not_5_out,
       not_6_out, or_1_out, or_2_out, or_3_out, or_4_out, or_5_out, or_6_out, or_7_out, or_8_out, or_9_out,
       or_10_out, xor_1_out, xor_2_out, xor_3_out, xor_4_out;

  // DipSwitch dipswitch_1: pin names not known; wires that end beside it: dipswitch_1_p1, dipswitch_1_p2, dipswitch_1_p3, dipswitch_1_p4
  not not_1 (not_1_out, in_48);
  four_bit_D_ff four_bit_d_ff_1 (
    ._1__nCLR(not_1_out), ._2__1Q(four_bit_d_ff_1__2__1q), ._4__1D(dipswitch_1_p1), ._5__2D(dipswitch_1_p2),
    ._7__2Q(four_bit_d_ff_1__7__2q), ._15__4Q(four_bit_d_ff_1__15__4q), ._13__4D(dipswitch_1_p4),
    ._12__3D(dipswitch_1_p3), ._10__3Q(four_bit_d_ff_1__10__3q), ._9__CLK(Q1));  // open: _3__1_Q, _6__2_Q, _8__GND, _16__Vcc, _14__4_Q, _11__3_Q
  four_bit_D_ff four_bit_d_ff_2 (
    ._1__nCLR(not_1_out), ._2__1Q(four_bit_d_ff_2__2__1q), ._4__1D(dipswitch_1_p1), ._5__2D(dipswitch_1_p2),
    ._7__2Q(four_bit_d_ff_2__7__2q), ._15__4Q(four_bit_d_ff_2__15__4q), ._13__4D(dipswitch_1_p4),
    ._12__3D(dipswitch_1_p3), ._10__3Q(four_bit_d_ff_2__10__3q), ._9__CLK(Q2));  // open: _3__1_Q, _6__2_Q, _8__GND, _16__Vcc, _14__4_Q, _11__3_Q
  four_bit_D_ff four_bit_d_ff_3 (
    ._1__nCLR(not_1_out), ._2__1Q(four_bit_d_ff_3__2__1q), ._4__1D(dipswitch_1_p1), ._5__2D(dipswitch_1_p2),
    ._7__2Q(four_bit_d_ff_3__7__2q), ._15__4Q(four_bit_d_ff_3__15__4q), ._13__4D(dipswitch_1_p4),
    ._12__3D(dipswitch_1_p3), ._10__3Q(four_bit_d_ff_3__10__3q), ._9__CLK(Q3));  // open: _3__1_Q, _6__2_Q, _8__GND, _16__Vcc, _14__4_Q, _11__3_Q
  four_bit_D_ff four_bit_d_ff_4 (
    ._1__nCLR(not_1_out), ._2__1Q(four_bit_d_ff_4__2__1q), ._4__1D(dipswitch_1_p1), ._5__2D(dipswitch_1_p2),
    ._7__2Q(four_bit_d_ff_4__7__2q), ._15__4Q(four_bit_d_ff_4__15__4q), ._13__4D(dipswitch_1_p4),
    ._12__3D(dipswitch_1_p3), ._10__3Q(four_bit_d_ff_4__10__3q), ._9__CLK(Q4));  // open: _3__1_Q, _6__2_Q, _8__GND, _16__Vcc, _14__4_Q, _11__3_Q
  four_bit_D_ff four_bit_d_ff_5 (
    ._1__nCLR(not_1_out), ._2__1Q(four_bit_d_ff_5__2__1q), ._4__1D(dipswitch_1_p1), ._5__2D(dipswitch_1_p2),
    ._7__2Q(four_bit_d_ff_5__7__2q), ._15__4Q(four_bit_d_ff_5__15__4q), ._13__4D(dipswitch_1_p4),
    ._12__3D(dipswitch_1_p3), ._10__3Q(four_bit_d_ff_5__10__3q), ._9__CLK(Q5));  // open: _3__1_Q, _6__2_Q, _8__GND, _16__Vcc, _14__4_Q, _11__3_Q
  four_bit_D_ff four_bit_d_ff_6 (
    ._1__nCLR(not_1_out), ._2__1Q(four_bit_d_ff_6__2__1q), ._4__1D(dipswitch_1_p1), ._5__2D(dipswitch_1_p2),
    ._7__2Q(four_bit_d_ff_6__7__2q), ._15__4Q(four_bit_d_ff_6__15__4q), ._13__4D(dipswitch_1_p4),
    ._12__3D(dipswitch_1_p3), ._10__3Q(four_bit_d_ff_6__10__3q), ._9__CLK(Q6));  // open: _3__1_Q, _6__2_Q, _8__GND, _16__Vcc, _14__4_Q, _11__3_Q
  four_bit_D_ff four_bit_d_ff_7 (
    ._1__nCLR(not_1_out), ._2__1Q(four_bit_d_ff_7__2__1q), ._4__1D(dipswitch_1_p1), ._5__2D(dipswitch_1_p2),
    ._7__2Q(four_bit_d_ff_7__7__2q), ._15__4Q(four_bit_d_ff_7__15__4q), ._13__4D(dipswitch_1_p4),
    ._12__3D(dipswitch_1_p3), ._10__3Q(four_bit_d_ff_7__10__3q), ._9__CLK(Q7));  // open: _3__1_Q, _6__2_Q, _8__GND, _16__Vcc, _14__4_Q, _11__3_Q
  four_bit_D_ff four_bit_d_ff_8 (
    ._1__nCLR(not_1_out), ._2__1Q(four_bit_d_ff_8__2__1q), ._4__1D(dipswitch_1_p1), ._5__2D(dipswitch_1_p2),
    ._7__2Q(four_bit_d_ff_8__7__2q), ._15__4Q(four_bit_d_ff_8__15__4q), ._13__4D(dipswitch_1_p4),
    ._12__3D(dipswitch_1_p3), ._10__3Q(four_bit_d_ff_8__10__3q), ._9__CLK(Q8));  // open: _3__1_Q, _6__2_Q, _8__GND, _16__Vcc, _14__4_Q, _11__3_Q
  four_bit_D_ff four_bit_d_ff_9 (
    ._1__nCLR(not_1_out), ._2__1Q(four_bit_d_ff_9__2__1q), ._4__1D(dipswitch_1_p1), ._5__2D(dipswitch_1_p2),
    ._7__2Q(four_bit_d_ff_9__7__2q), ._15__4Q(four_bit_d_ff_9__15__4q), ._13__4D(dipswitch_1_p4),
    ._12__3D(dipswitch_1_p3), ._10__3Q(four_bit_d_ff_9__10__3q), ._9__CLK(Q9));  // open: _3__1_Q, _6__2_Q, _8__GND, _16__Vcc, _14__4_Q, _11__3_Q
  four_bit_D_ff four_bit_d_ff_10 (
    ._1__nCLR(not_1_out), ._2__1Q(four_bit_d_ff_10__2__1q), ._4__1D(dipswitch_1_p1), ._5__2D(dipswitch_1_p2),
    ._7__2Q(four_bit_d_ff_10__7__2q), ._15__4Q(four_bit_d_ff_10__15__4q), ._13__4D(dipswitch_1_p4),
    ._12__3D(dipswitch_1_p3), ._10__3Q(four_bit_d_ff_10__10__3q), ._9__CLK(Q10));  // open: _3__1_Q, _6__2_Q, _8__GND, _16__Vcc, _14__4_Q, _11__3_Q
  _16_1_MUX u_16_1_mux_1 (
    ._1__E7(four_bit_d_ff_7__2__1q), ._2__E6(four_bit_d_ff_6__2__1q), ._3__E5(four_bit_d_ff_5__2__1q),
    ._4__E4(four_bit_d_ff_4__2__1q), ._5__E3(four_bit_d_ff_3__2__1q), ._6__E2(four_bit_d_ff_2__2__1q),
    ._7__E1(four_bit_d_ff_1__2__1q), ._8__E0(_0_2), ._9__nG(Clear___0), ._10__W(Correct_Answer),
    ._11__D(out_75), ._23__E8(four_bit_d_ff_10__2__1q), ._22__E9(four_bit_d_ff_9__2__1q),
    ._21__E10(four_bit_d_ff_8__2__1q), ._20__E11(_0), ._19__E12(_0), ._18__E13(_0), ._17__E14(_0),
    ._16__E15(_0), ._15__A(out_72), ._14__B(Question_Number), ._13__C(out_74));  // open: _12__GND, _24__Vcc
  _16_1_MUX u_16_1_mux_2 (
    ._1__E7(four_bit_d_ff_7__7__2q), ._2__E6(four_bit_d_ff_6__7__2q), ._3__E5(four_bit_d_ff_5__7__2q),
    ._4__E4(four_bit_d_ff_4__7__2q), ._5__E3(four_bit_d_ff_3__7__2q), ._6__E2(four_bit_d_ff_2__7__2q),
    ._7__E1(four_bit_d_ff_1__7__2q), ._8__E0(_0_6), ._9__nG(Clear___0), ._10__W(out_56), ._11__D(out_75),
    ._23__E8(four_bit_d_ff_8__7__2q), ._22__E9(four_bit_d_ff_9__7__2q), ._21__E10(four_bit_d_ff_10__7__2q),
    ._20__E11(_0_5), ._19__E12(_0_5), ._18__E13(_0_5), ._17__E14(_0_5), ._16__E15(_0_5), ._15__A(out_72),
    ._14__B(Question_Number), ._13__C(out_74));  // open: _12__GND, _24__Vcc
  _16_1_MUX u_16_1_mux_3 (
    ._1__E7(four_bit_d_ff_7__10__3q), ._2__E6(four_bit_d_ff_6__10__3q), ._3__E5(four_bit_d_ff_5__10__3q),
    ._4__E4(four_bit_d_ff_4__10__3q), ._5__E3(four_bit_d_ff_3__10__3q), ._6__E2(four_bit_d_ff_2__10__3q),
    ._7__E1(four_bit_d_ff_1__10__3q), ._8__E0(_0_13), ._9__nG(Clear___0), ._10__W(out_57), ._11__D(out_75),
    ._23__E8(four_bit_d_ff_8__10__3q), ._22__E9(four_bit_d_ff_9__10__3q),
    ._21__E10(four_bit_d_ff_10__10__3q), ._20__E11(_0_12), ._19__E12(_0_12), ._18__E13(_0_12),
    ._17__E14(_0_12), ._16__E15(_0_12), ._15__A(out_72), ._14__B(Question_Number), ._13__C(out_74));  // open: _12__GND, _24__Vcc
  _16_1_MUX u_16_1_mux_4 (
    ._1__E7(four_bit_d_ff_7__15__4q), ._2__E6(four_bit_d_ff_6__15__4q), ._3__E5(four_bit_d_ff_5__15__4q),
    ._4__E4(four_bit_d_ff_4__15__4q), ._5__E3(four_bit_d_ff_3__15__4q), ._6__E2(four_bit_d_ff_2__15__4q),
    ._7__E1(four_bit_d_ff_1__15__4q), ._8__E0(_0_19), ._9__nG(Clear___0), ._10__W(out_59), ._11__D(out_75),
    ._23__E8(four_bit_d_ff_8__15__4q), ._22__E9(four_bit_d_ff_9__15__4q),
    ._21__E10(four_bit_d_ff_10__15__4q), ._20__E11(_0_17), ._19__E12(_0_17), ._18__E13(_0_17),
    ._17__E14(_0_17), ._16__E15(_0_17), ._15__A(out_72), ._14__B(Question_Number), ._13__C(out_74));  // open: _12__GND, _24__Vcc
  or or_1 (or_1_out, n4_bit_magnitude_comparator_1__5__a_b_out, n4_bit_magnitude_comparator_1__7__a_b_out);
  LED False_Answer_Indicator (.in(or_1_out));
  _4_bit_Magnitude_Comparator u_4_bit_magnitude_comparator_1 (
    ._15__A3(out_59), ._1__B3(in_26), ._13__A2(out_57), ._14__B2(in_25), ._2__A_B_in(in_9),
    ._3__A_B_in(in_12), ._4__A_B_in(in_15), ._12__A1(out_56), ._11__B1(in_24), ._10__A0(Correct_Answer),
    ._9__B0(in_23), ._5__A_B_out(n4_bit_magnitude_comparator_1__5__a_b_out),
    ._6__A_B_out(n4_bit_magnitude_comparator_1__6__a_b_out),
    ._7__A_B_out(n4_bit_magnitude_comparator_1__7__a_b_out));  // open: _16__Vcc, _8__GND
  _12_Stage_Binary_Ripple_Counter u_12_stage_binary_ripple_counter_1 (
    ._5__Q4(out_75), ._6__Q3(out_74), ._7__Q2(Question_Number), ._11__RESET(RESET), .\_10__nφ (not_3_out),
    ._9__Q1(out_72));  // open: _1__Q12, _2__Q6, _3__Q5, _4__Q7, _8__Vss, _16__Vdd, _15__Q11, _14__Q10, _13__Q8, _12__Q9
  not not_2 (not_2_out, n4_bit_magnitude_comparator_1__6__a_b_out);
  and and_1 (and_1_out, n4_bit_magnitude_comparator_1__6__a_b_out, Move_to_next_Question);
  not not_3 (not_3_out, Move_to_next_Question);
  and and_2 (and_2_out, Move_to_next_Question, not_2_out);
  not not_4 (not_4_out, and_1_out);
  _12_Stage_Binary_Ripple_Counter u_12_stage_binary_ripple_counter_2 (
    ._5__Q4(out_65), ._6__Q3(Result), ._7__Q2(out_61), ._11__RESET(RESET), .\_10__nφ (not_4_out),
    ._9__Q1(out_58));  // open: _1__Q12, _2__Q6, _3__Q5, _4__Q7, _8__Vss, _16__Vdd, _15__Q11, _14__Q10, _13__Q8, _12__Q9
  _4_bit_Magnitude_Comparator u_4_bit_magnitude_comparator_2 (
    ._15__A3(out_75), ._1__B3(_0_21), ._13__A2(out_74), ._14__B2(_0_20), ._2__A_B_in(_0_15),
    ._3__A_B_in(_1_6), ._4__A_B_in(_0_16), ._12__A1(Question_Number), ._11__B1(_0_18), ._10__A0(out_72),
    ._9__B0(_1_7), ._6__A_B_out(n4_bit_magnitude_comparator_2__6__a_b_out));  // open: _16__Vcc, _8__GND, _5__A_B_out, _7__A_B_out
  J_K_Flip_Flop #(.Pre_Clr_Positions("LEGACY"), .enable("true"), .NewFFLayout("false")) j_k_ff_1 (
    .J(_1), .clk(and_2_out), .K(_1), .Q(out_51), .Qn(j_k_ff_1_qn), .reset(or_2_out));  // open: preset, en
  or or_2 (or_2_out, RESET, and_3_out);
  and and_3 (and_3_out, n4_bit_magnitude_comparator_1__6__a_b_out, n4_bit_magnitude_comparator_2__6__a_b_out);
  J_K_Flip_Flop #(.Pre_Clr_Positions("LEGACY"), .enable("true"), .NewFFLayout("false")) j_k_ff_2 (
    .J(_1), .clk(j_k_ff_1_qn), .K(_1), .Q(out_52), .Qn(j_k_ff_2_qn), .reset(or_2_out));  // open: preset, en
  xor xor_1 (xor_1_out, _1_2, out_51);
  _4_bit_Adder BCD_Adder (
    ._1__A4(out_65), .\_2__Σ3 (\BCD_Adder__2__σ3 ), ._3__A3(Result), ._4__B3(_1_5),
    .\_6__Σ2 (\BCD_Adder__6__σ2 ), ._7__B2(_1_4), ._8__A2(out_61), ._16__B4(_0_14),
    .\_15__Σ4 (\BCD_Adder__15__σ4 ), ._14__C4(BCD_Adder__14__c4), ._13__C0(in_38), ._11__B1(_0_11),
    ._10__A1(out_58), .\_9__Σ1 (\BCD_Adder__9__σ1 ));  // open: _5__Vcc, _12__GND
  J_K_Flip_Flop #(.Pre_Clr_Positions("LEGACY"), .enable("true"), .NewFFLayout("false")) j_k_ff_3 (
    .J(_1), .clk(j_k_ff_2_qn), .K(_1), .Q(out_53), .Qn(j_k_ff_3_qn), .reset(or_2_out));  // open: preset, en
  xor xor_2 (xor_2_out, _1_2, out_52);
  not not_5 (not_5_out, BCD_Adder__14__c4);
  xor xor_3 (xor_3_out, _1_2, out_53);
  and and_4 (and_4_out, out_58, not_5_out);
  and and_5 (and_5_out, out_61, not_5_out);
  and and_6 (and_6_out, Result, not_5_out);
  and and_7 (and_7_out, out_65, not_5_out);
  and and_8 (and_8_out, \BCD_Adder__9__σ1 , BCD_Adder__14__c4);
  and and_9 (and_9_out, \BCD_Adder__6__σ2 , BCD_Adder__14__c4);
  and and_10 (and_10_out, \BCD_Adder__2__σ3 , BCD_Adder__14__c4);
  and and_11 (and_11_out, \BCD_Adder__15__σ4 , BCD_Adder__14__c4);
  J_K_Flip_Flop #(.Pre_Clr_Positions("LEGACY"), .enable("true"), .NewFFLayout("false")) j_k_ff_4 (
    .J(_1), .clk(j_k_ff_3_qn), .K(_1), .Q(out_54), .reset(or_2_out));  // open: Qn, preset, en
  xor xor_4 (xor_4_out, _1_2, out_54);
  or or_3 (or_3_out, and_4_out, and_8_out);
  or or_4 (or_4_out, and_5_out, and_9_out);
  or or_5 (or_5_out, and_6_out, and_10_out);
  or or_6 (or_6_out, and_7_out, and_11_out);
  _4_bit_Adder u_4_bit_adder_1 (
    ._1__A4(out_65), .\_2__Σ3 (\n4_bit_adder_1__2__σ3 ), ._3__A3(Result), ._4__B3(xor_3_out),
    .\_6__Σ2 (\n4_bit_adder_1__6__σ2 ), ._7__B2(xor_2_out), ._8__A2(out_61), ._16__B4(xor_4_out),
    .\_15__Σ4 (\n4_bit_adder_1__15__σ4 ), ._14__C4(out_67), ._13__C0(_1_2), ._11__B1(xor_1_out),
    ._10__A1(out_58), .\_9__Σ1 (\n4_bit_adder_1__9__σ1 ));  // open: _5__Vcc, _12__GND
  BCD_to_7_segment_display_decoder bcd_to_7_segment_display_decoder_1 (
    .A0(_0_10), .A1(_0_10), .A2(_0_10), .A3(BCD_Adder__14__c4), .a(bcd_to_7_segment_display_decoder_1_a),
    .b(bcd_to_7_segment_display_decoder_1_b), .c(bcd_to_7_segment_display_decoder_1_c),
    .d(bcd_to_7_segment_display_decoder_1_d), .e(bcd_to_7_segment_display_decoder_1_e),
    .f(bcd_to_7_segment_display_decoder_1_f), .g(bcd_to_7_segment_display_decoder_1_g));
  _7_Segment_Display u_7_segment_display_1 (
    .g(bcd_to_7_segment_display_decoder_1_g), .f(bcd_to_7_segment_display_decoder_1_f),
    .a(bcd_to_7_segment_display_decoder_1_a), .b(bcd_to_7_segment_display_decoder_1_b),
    .e(bcd_to_7_segment_display_decoder_1_e), .d(bcd_to_7_segment_display_decoder_1_d),
    .c(bcd_to_7_segment_display_decoder_1_c), .dp(1'b0));
  and and_12 (out_60, \n4_bit_adder_1__9__σ1 , out_67);
  and and_13 (out_62, out_67, \n4_bit_adder_1__6__σ2 );
  and and_14 (out_64, out_67, \n4_bit_adder_1__2__σ3 );
  and and_15 (out_66, \n4_bit_adder_1__15__σ4 , out_67);
  BCD_to_7_segment_display_decoder bcd_to_7_segment_display_decoder_2 (
    .A0(or_6_out), .A1(or_5_out), .A2(or_4_out), .A3(or_3_out), .a(bcd_to_7_segment_display_decoder_2_a),
    .b(bcd_to_7_segment_display_decoder_2_b), .c(bcd_to_7_segment_display_decoder_2_c),
    .d(bcd_to_7_segment_display_decoder_2_d), .e(bcd_to_7_segment_display_decoder_2_e),
    .f(bcd_to_7_segment_display_decoder_2_f), .g(bcd_to_7_segment_display_decoder_2_g));
  _7_Segment_Display u_7_segment_display_2 (
    .g(bcd_to_7_segment_display_decoder_2_g), .f(bcd_to_7_segment_display_decoder_2_f),
    .a(bcd_to_7_segment_display_decoder_2_a), .b(bcd_to_7_segment_display_decoder_2_b),
    .e(bcd_to_7_segment_display_decoder_2_e), .d(bcd_to_7_segment_display_decoder_2_d),
    .c(bcd_to_7_segment_display_decoder_2_c), .dp(1'b0));
  _4_bit_Adder BCD_Adder_2 (
    ._1__A4(out_66), .\_2__Σ3 (\BCD_Adder_2__2__σ3 ), ._3__A3(out_64), ._4__B3(_0_7),
    .\_6__Σ2 (\BCD_Adder_2__6__σ2 ), ._7__B2(_1_3), ._8__A2(out_62), ._16__B4(_0_8),
    .\_15__Σ4 (\BCD_Adder_2__15__σ4 ), ._14__C4(BCD_Adder_2__14__c4), ._13__C0(_0_9), ._11__B1(_0_4),
    ._10__A1(out_60), .\_9__Σ1 (\BCD_Adder_2__9__σ1 ));  // open: _5__Vcc, _12__GND
  and and_16 (and_16_out, out_60, not_6_out);
  and and_17 (and_17_out, out_62, not_6_out);
  and and_18 (and_18_out, out_64, not_6_out);
  and and_19 (and_19_out, out_66, not_6_out);
  and and_20 (and_20_out, \BCD_Adder_2__9__σ1 , BCD_Adder_2__14__c4);
  and and_21 (and_21_out, \BCD_Adder_2__6__σ2 , BCD_Adder_2__14__c4);
  and and_22 (and_22_out, \BCD_Adder_2__2__σ3 , BCD_Adder_2__14__c4);
  and and_23 (and_23_out, \BCD_Adder_2__15__σ4 , BCD_Adder_2__14__c4);
  not not_6 (not_6_out, BCD_Adder_2__14__c4);
  or or_7 (or_7_out, and_16_out, and_20_out);
  or or_8 (or_8_out, and_17_out, and_21_out);
  or or_9 (or_9_out, and_18_out, and_22_out);
  or or_10 (or_10_out, and_19_out, and_23_out);
  BCD_to_7_segment_display_decoder bcd_to_7_segment_display_decoder_3 (
    .A0(_0_3), .A1(_0_3), .A2(_0_3), .A3(BCD_Adder_2__14__c4), .a(bcd_to_7_segment_display_decoder_3_a),
    .b(bcd_to_7_segment_display_decoder_3_b), .c(bcd_to_7_segment_display_decoder_3_c),
    .d(bcd_to_7_segment_display_decoder_3_d), .e(bcd_to_7_segment_display_decoder_3_e),
    .f(bcd_to_7_segment_display_decoder_3_f), .g(bcd_to_7_segment_display_decoder_3_g));
  _7_Segment_Display u_7_segment_display_3 (
    .g(bcd_to_7_segment_display_decoder_3_g), .f(bcd_to_7_segment_display_decoder_3_f),
    .a(bcd_to_7_segment_display_decoder_3_a), .b(bcd_to_7_segment_display_decoder_3_b),
    .e(bcd_to_7_segment_display_decoder_3_e), .d(bcd_to_7_segment_display_decoder_3_d),
    .c(bcd_to_7_segment_display_decoder_3_c), .dp(1'b0));
  BCD_to_7_segment_display_decoder bcd_to_7_segment_display_decoder_4 (
    .A0(or_10_out), .A1(or_9_out), .A2(or_8_out), .A3(or_7_out), .a(bcd_to_7_segment_display_decoder_4_a),
    .b(bcd_to_7_segment_display_decoder_4_b), .c(bcd_to_7_segment_display_decoder_4_c),
    .d(bcd_to_7_segment_display_decoder_4_d), .e(bcd_to_7_segment_display_decoder_4_e),
    .f(bcd_to_7_segment_display_decoder_4_f), .g(bcd_to_7_segment_display_decoder_4_g));
  _7_Segment_Display u_7_segment_display_4 (
    .g(bcd_to_7_segment_display_decoder_4_g), .f(bcd_to_7_segment_display_decoder_4_f),
    .a(bcd_to_7_segment_display_decoder_4_a), .b(bcd_to_7_segment_display_decoder_4_b),
    .e(bcd_to_7_segment_display_decoder_4_e), .d(bcd_to_7_segment_display_decoder_4_d),
    .c(bcd_to_7_segment_display_decoder_4_c), .dp(1'b0));

  assign out_68 = in_23;
  assign out_69 = in_24;
  assign out_70 = in_25;
  assign out_71 = in_26;

  // Notes on the sheet:
  //   LDR Inputs
  //   Scanned Answer
  //   2. Input Configuration:
  //   4. DIP Switch Configuration:
  //   6. LDR Input Procedure:
  //   DIGITAL LOGIC APPROACH TO OMR IMPLEMENTATION
  //     - Repeat this process for all 10 questions.
  //   INSTRUCTIONS:
  //   1. Reset the Circuit: Set the RESET button to 0 to initialize the entire circuit.
  //   3. Clock Settings: Ensure all clocks are set to 1 for each question.
  //      - Then, set the clock for that specific question to 0, and back to 1. 
  //   7. Final Reset: After scanning all 10 questions, set the reset button back to 0.
  //      - If the correct answer for Question 1 is A, turn off DIP switch A and turn on all other switches. 
  //      - Press 1 in the LDR input for the question. The score will increment/decrement after this action.
  //      - After reviewing the score, reset the LDR input to 0, then press 1 again for the next question. 
  //   OVERALL CIRCUIT
  //   - For any label marked zero or one, set the corresponding inputs in comparators, BCD adder, enable, and clear for multiplexers and wherever applicable.
  //   5. Set LDR Input for Scanned Answer Button: For each question, activate one of the input buttons (A, B, C, or D) corresponding to the student response.
  //      - Ensure that the student response for the next question is set in the LDR input for scanned answers before moving to the next question.
  //   Total number of Correct Responses
  //   TEAM ID:
  //   ATHARVA ATUL REGE    231CS114
  //   B SRIRAM                            231CS116
  //   SHREYAS LAL                    231CS156
  //   Final Score with Negative Marking considered
endmodule

// 4-bit Flip-flop
module four_bit_D_ff (
  input  _1__nCLR,
  input  _4__1D,
  input  _13__4D,
  input  _5__2D,
  input  _12__3D,
  input  _9__CLK,
  output _16__Vcc,
  output _2__1Q,
  output _15__4Q,
  output _3__1_Q,
  output _14__4_Q,
  output _6__2_Q,
  output _11__3_Q,
  output _7__2Q,
  output _10__3Q,
  output _8__GND
);

  wire not_1_out;

  not not_1 (not_1_out, _1__nCLR);
  D_Flip_Flop #(.Pre_Clr_Positions("LEGACY"), .enable("true"), .NewFFLayout("false")) d_ff_1 (
    .clk(_9__CLK), .D(_4__1D), .Q(_2__1Q), .Qn(_3__1_Q), .reset(not_1_out));  // open: preset, en
  D_Flip_Flop #(.Pre_Clr_Positions("LEGACY"), .enable("true"), .NewFFLayout("false")) d_ff_2 (
    .clk(_9__CLK), .D(_5__2D), .Q(_7__2Q), .Qn(_6__2_Q), .reset(not_1_out));  // open: preset, en
  D_Flip_Flop #(.Pre_Clr_Positions("LEGACY"), .enable("true"), .NewFFLayout("false")) d_ff_3 (
    .clk(_9__CLK), .D(_13__4D), .Q(_15__4Q), .Qn(_14__4_Q), .reset(not_1_out));  // open: preset, en
  D_Flip_Flop #(.Pre_Clr_Positions("LEGACY"), .enable("true"), .NewFFLayout("false")) d_ff_4 (
    .clk(_9__CLK), .D(_12__3D), .Q(_10__3Q), .Qn(_11__3_Q), .reset(not_1_out));  // open: preset, en

  assign _8__GND = 1'b0;
  assign _16__Vcc = 1'b1;
endmodule

// 16:1 MUX
module _16_1_MUX (
  input  _1__E7,
  input  _2__E6,
  input  _23__E8,
  input  _3__E5,
  input  _22__E9,
  input  _4__E4,
  input  _21__E10,
  input  _5__E3,
  input  _20__E11,
  input  _6__E2,
  input  _19__E12,
  input  _7__E1,
  input  _18__E13,
  input  _8__E0,
  input  _17__E14,
  input  _9__nG,
  input  _16__E15,
  input  _15__A,
  input  _11__D,
  input  _14__B,
  input  _13__C,
  output _24__Vcc,
  output _10__W,
  output _12__GND
);

  wire multiplexer_1_out, not_2_out;

  not not_1 (_10__W, multiplexer_1_out);
  not not_2 (not_2_out, _9__nG);
  Multiplexer #(.select(4), .disabled(0)) multiplexer_1 (
    .in0(_8__E0), .in1(_7__E1), .in2(_6__E2), .in3(_5__E3), .in4(_4__E4), .in5(_3__E5), .in6(_2__E6),
    .in7(_1__E7), .in8(_23__E8), .in9(_22__E9), .in10(_21__E10), .in11(_20__E11), .in12(_19__E12),
    .in13(_18__E13), .in14(_17__E14), .in15(_16__E15), .out(multiplexer_1_out),
    .sel({_11__D, _13__C, _14__B, _15__A}), .en(not_2_out));

  assign _12__GND = 1'b0;
  assign _24__Vcc = 1'b1;
endmodule

// Counter
module _12_Stage_Binary_Ripple_Counter (
  input  _11__RESET,
  input  \_10__nφ ,
  output _1__Q12,
  output _16__Vdd,
  output _2__Q6,
  output _15__Q11,
  output _3__Q5,
  output _14__Q10,
  output _4__Q7,
  output _13__Q8,
  output _5__Q4,
  output _12__Q9,
  output _6__Q3,
  output _7__Q2,
  output _8__Vss,
  output _9__Q1
);

  Counter #(.width(12), .max('hfff), .trigger("falling"), .behavior("old")) counter_1 (
    .Q({_1__Q12, _15__Q11, _14__Q10, _12__Q9, _13__Q8, _4__Q7, _2__Q6, _3__Q5, _5__Q4, _6__Q3, _7__Q2, _9__Q1}),
    .clk(\_10__nφ ), .clr(_11__RESET));  // open: load, D, count, carry, preset

  assign _8__Vss = 1'b0;
  assign _16__Vdd = 1'b1;
endmodule

// Magnitude Comparator
module _4_bit_Magnitude_Comparator (
  input  _15__A3,
  input  _1__B3,
  input  _13__A2,
  input  _14__B2,
  input  _2__A_B_in,
  input  _3__A_B_in,
  input  _4__A_B_in,
  input  _12__A1,
  input  _11__B1,
  input  _10__A0,
  input  _9__B0,
  output _16__Vcc,
  output _8__GND,
  output _5__A_B_out,
  output _6__A_B_out,
  output _7__A_B_out
);

  wire and_1_out, and_2_out, and_3_out, and_4_out, and_5_out, and_6_out, and_7_out, and_8_out, and_9_out,
       and_10_out, and_11_out, and_12_out, and_13_out, and_14_out, and_15_out, and_16_out, and_17_out,
       and_18_out, and_19_out, and_20_out, nand_1_out, nand_2_out, nand_3_out, nand_4_out, nor_1_out,
       nor_2_out, nor_3_out, nor_4_out;

  nand nand_1 (nand_1_out, _15__A3, _1__B3);
  nand nand_2 (nand_2_out, _13__A2, _14__B2);
  nand nand_3 (nand_3_out, _12__A1, _11__B1);
  nand nand_4 (nand_4_out, _10__A0, _9__B0);
  and and_1 (and_1_out, _15__A3, nand_1_out);
  nor nor_1 (nor_1_out, and_1_out, and_2_out);
  and and_2 (and_2_out, nand_1_out, _1__B3);
  and and_3 (and_3_out, _13__A2, nand_2_out);
  nor nor_2 (nor_2_out, and_3_out, and_4_out);
  and and_4 (and_4_out, nand_2_out, _14__B2);
  and and_5 (and_5_out, _12__A1, nand_3_out);
  nor nor_3 (nor_3_out, and_5_out, and_6_out);
  and and_6 (and_6_out, nand_3_out, _11__B1);
  and and_7 (and_7_out, _10__A0, nand_4_out);
  nor nor_4 (nor_4_out, and_7_out, and_8_out);
  and and_8 (and_8_out, nand_4_out, _9__B0);
  and and_9 (and_9_out, _1__B3, nand_1_out);
  and and_10 (and_10_out, _14__B2, nand_2_out, nor_1_out);
  and and_11 (and_11_out, _11__B1, nand_3_out, nor_1_out, nor_2_out);
  and and_12 (and_12_out, _9__B0, nand_4_out, nor_1_out, nor_2_out, nor_3_out);
  and and_13 (and_13_out, nor_1_out, nor_2_out, nor_3_out, nor_4_out, _2__A_B_in);
  and and_14 (and_14_out, nor_1_out, nor_2_out, nor_3_out, nor_4_out, _3__A_B_in);
  and and_15 (and_15_out, _3__A_B_in, nor_4_out, nor_3_out, nor_2_out, nor_1_out);
  and and_16 (and_16_out, _4__A_B_in, nor_4_out, nor_3_out, nor_2_out, nor_1_out);
  and and_17 (and_17_out, nor_3_out, nor_2_out, nor_1_out, nand_4_out, _10__A0);
  and and_18 (and_18_out, nor_2_out, nor_1_out, nand_3_out, _12__A1);
  and and_19 (and_19_out, nor_1_out, nand_2_out, _13__A2);
  and and_20 (and_20_out, nand_1_out, _15__A3);
  nor nor_5 (_5__A_B_out, and_9_out, and_10_out, and_11_out, and_12_out, and_13_out, and_14_out);
  and and_21 (_6__A_B_out, nor_1_out, nor_2_out, _3__A_B_in, nor_3_out, nor_4_out);
  nor nor_6 (_7__A_B_out, and_15_out, and_16_out, and_17_out, and_18_out, and_19_out, and_20_out);

  assign _8__GND = 1'b0;
  assign _16__Vcc = 1'b1;
endmodule

module _4_bit_Adder (
  input  _1__A4,
  input  _16__B4,
  input  _3__A3,
  input  _4__B3,
  input  _13__C0,
  input  _11__B1,
  input  _7__B2,
  input  _10__A1,
  input  _8__A2,
  output \_2__Σ3 ,
  output \_15__Σ4 ,
  output _14__C4,
  output _5__Vcc,
  output _12__GND,
  output \_6__Σ2 ,
  output \_9__Σ1 
);

  Adder #(.width(4)) adder_1 (
    .a({_1__A4, _3__A3, _8__A2, _10__A1}), .b({_16__B4, _4__B3, _7__B2, _11__B1}),
    .out({\_15__Σ4 , \_2__Σ3 , \_6__Σ2 , \_9__Σ1 }), .cin(_13__C0), .cout(_14__C4));

  assign _5__Vcc = 1'b1;
  assign _12__GND = 1'b0;
endmodule

module BCD_to_7_segment_display_decoder (
  input  A0,
  input  A1,
  input  A2,
  input  A3,
  output a,
  output b,
  output c,
  output d,
  output e,
  output f,
  output g
);

  wire and_1_out, and_2_out, and_3_out, and_4_out, and_5_out, and_6_out, and_7_out, and_8_out, and_9_out,
       and_10_out, and_11_out, and_12_out, and_13_out, and_14_out, and_15_out, and_16_out, not_1_out,
       not_2_out, not_3_out, not_4_out, not_5_out, not_6_out, not_7_out, not_8_out, not_9_out, not_10_out,
       not_11_out, not_12_out, not_13_out, not_14_out, not_15_out, not_16_out, not_17_out, not_18_out,
       not_19_out, not_20_out, not_21_out;

  not not_1 (not_1_out, A1);
  and and_1 (and_1_out, not_1_out, not_2_out);
  not not_2 (not_2_out, A3);
  and and_2 (and_2_out, A1, A3);
  not not_3 (not_3_out, A1);
  not not_4 (not_4_out, A2);
  and and_3 (and_3_out, not_4_out, not_5_out);
  not not_5 (not_5_out, A3);
  and and_4 (and_4_out, A2, A3);
  not not_6 (not_6_out, A2);
  or or_1 (c, not_6_out, A3, A1);
  not not_7 (not_7_out, A1);
  and and_5 (and_5_out, not_7_out, not_8_out);
  not not_8 (not_8_out, A3);
  not not_9 (not_9_out, A1);
  and and_6 (and_6_out, not_9_out, A2);
  and and_7 (and_7_out, A2, not_10_out);
  not not_10 (not_10_out, A3);
  and and_8 (and_8_out, A1, not_11_out, A3);
  not not_11 (not_11_out, A2);
  not not_12 (not_12_out, A1);
  and and_9 (and_9_out, not_12_out, not_13_out);
  not not_13 (not_13_out, A3);
  and and_10 (and_10_out, A2, not_14_out);
  not not_14 (not_14_out, A3);
  not not_15 (not_15_out, A2);
  and and_11 (and_11_out, not_15_out, not_16_out);
  not not_16 (not_16_out, A3);
  and and_12 (and_12_out, A1, not_17_out);
  not not_17 (not_17_out, A2);
  and and_13 (and_13_out, A1, not_18_out);
  not not_18 (not_18_out, A3);
  not not_19 (not_19_out, A1);
  and and_14 (and_14_out, not_19_out, A2);
  and and_15 (and_15_out, A1, not_20_out);
  not not_20 (not_20_out, A2);
  and and_16 (and_16_out, A1, not_21_out);
  not not_21 (not_21_out, A3);
  or or_2 (a, and_1_out, A2, and_2_out, A0);
  or or_3 (b, not_3_out, and_3_out, and_4_out);
  or or_4 (d, and_5_out, and_6_out, and_7_out, and_8_out, A0);
  or or_5 (e, and_9_out, and_10_out);
  or or_6 (f, and_11_out, and_12_out, and_13_out, A0);
  or or_7 (g, and_14_out, and_15_out, and_16_out, A0);
endmodule
